# Fritzing sketch lagtest (saved by Fritzing 0.7.10b)

parts:
  Arduino2 = Arduino
  Q1 = NPN-Transistor [package="TO92 [THT]"]

nets:
  N1: Arduino2.GND, Q1.C
  N2: Arduino2.+5V, Q1.B
  N3: Arduino2.A0, Q1.E

// code stored in the sketch: Blink.ino
/*
  Blink
  Turns on an LED on for one second, then off for one second, repeatedly.
 
  This example code is in the public domain.
 */

void setup() {                
  // initialize the digital pin as an output.
  // Pin 13 has an LED connected on most Arduino boards:
  pinMode(13, OUTPUT);     
}

void loop() {
  digitalWrite(13, HIGH);   // set the LED on
  delay(1000);              // wait for a second
  digitalWrite(13, LOW);    // set the LED off
  delay(1000);              // wait for a second
}
